# Fritzing sketch Monster-in-a-box (saved by Fritzing 0.9.3b)

parts:
  Raspberry_Pi_1 = Raspberry Pi 3 [part_number=RPI-3-V1.2]
  U2 = 4-Channel 5v Relay Shield [package=relay-4ch5v10a]
  L1 = Solenoid
  L2 = Solenoid
  SPKR1 = Loudspeaker  # not connected

nets:
  GND: Raspberry_Pi_1.GND, U2.GND
  5V: Raspberry_Pi_1.5V, U2.VCC, U2.IN4
  N1: U2.K1-Off, L1.pin1
  N2: U2.K1-On, L1.pin2
  N3: U2.K2-Off, L2.pin1
  N4: U2.K2-On, L2.pin2

notes:
  Door Lock Actuators
  Fog Machine
  4 Channel Relay
  RaspberryPi 3

custom parts:
  4-Channel 5v Relay Shield: 4 Channel 5v Relay Shield w. 2x SPD-06VDC-SD-C
